# Fritzing sketch Aprinderea unui LED cu modulul SN7407 logica NORMALA (saved by Fritzing 0.9.3b)
breadboards: 1

parts:
  SN7407 = H-Bridge [package=THT]
  V1 = DC Power [voltage=5]
  R1 = Resistor [tolerance=±5% resistance=866 package=THT]
  LED1 = LED - 5mm [color="Red (633nm)" package="5 mm [THT]"]

nets:
  N1: SN7407.2A, SN7407.GND, LED1.cathode
  N2: SN7407.2Y, V1.V+, R1.Pin_1, LED1.anode
  N3: SN7407.VCC, R1.Pin_0

custom parts:
  H-Bridge: Quadruple Half H-Bridge Motor Driver. Drive two motors with 1.1A with this chip. (SN754410 data sheet from TI here http://focus.ti.com/lit/ds/symlink/sn754410.pdf )
