# Fritzing sketch Aprinderea unui LED cu modulul SN7407 logica inversata (saved by Fritzing 0.9.3b)
breadboards: 1

parts:
  R1 = Resistor [tolerance=±5% resistance=866 package=THT]
  V1 = DC Power [voltage=5]
  LED1 = smd LED [color="Red (633nm)" package="0805 [SMD]"]
  SN7407 = H-Bridge [package=THT]

nets:
  N1: R1.Pin_1, V1.V+, SN7407.VCC
  N2: V1.V-, SN7407.1A, SN7407.GND
  N3: LED1.cathode, SN7407.1Y

custom parts:
  H-Bridge: Quadruple Half H-Bridge Motor Driver. Drive two motors with 1.1A with this chip. (SN754410 data sheet from TI here http://focus.ti.com/lit/ds/symlink/sn754410.pdf )
