# Fritzing sketch Aprinderea unui LED direct de la sursa de 5v (saved by Fritzing 0.9.3b)
breadboards: 1

parts:
  LED1 = LED - 5mm [color="Red (633nm)" package="5 mm [THT]"]
  R1 = Resistor [tolerance=±5% resistance=866 package=THT]
  V1 = DC Power [voltage=5]

nets:
  N1: LED1.cathode, R1.Pin_0
  N2: LED1.anode, V1.V+
  N3: R1.Pin_1, V1.V-
