# Fritzing sketch Controlul unui LED folosind un push button (saved by Fritzing 0.9.3b)
breadboards: 1

parts:
  SN7407 = H-Bridge [package=THT]
  V1 = DC Power [voltage=5]
  R1 = Resistor [tolerance=±5% resistance=866 package=THT]
  LED1 = LED - 5mm [color="Red (633nm)" package="5 mm [THT]"]
  R2 = Resistor [tolerance=±5% resistance=866 package=THT]
  S1 = Square Pushbutton

nets:
  N1: SN7407.3A, R2.Pin_0, S1.leg1
  N2: SN7407.3Y, V1.V+, R1.Pin_1, LED1.anode
  N3: SN7407.GND, V1.V-, LED1.cathode, S1.leg0
  N4: SN7407.VCC, R1.Pin_0, R2.Pin_1

custom parts:
  H-Bridge: Quadruple Half H-Bridge Motor Driver. Drive two motors with 1.1A with this chip. (SN754410 data sheet from TI here http://focus.ti.com/lit/ds/symlink/sn754410.pdf )
